# Fritzing sketch skema_project (saved by Fritzing 1.0.6)

parts:
  부품1 = FC-28 Soil Hygrometer Module - Probe
  부품2 = FC-28 Soil Hygrometer Module
  U1 = NodeMCU V3.0

nets:
  N1: 부품1.POS, 부품2.POS
  N2: 부품1.NEG, 부품2.NEG
  N3: 부품2.VCC, U1.VU
  GND: 부품2.GND, U1.GND
  N4: 부품2.AO, U1.A0

custom parts:
  FC-28 Soil Hygrometer Module - Probe: The FC-28 is a soil hygrometer module that uses the Texas Instruments LM393 comparator chip to provide an analog measurement of soil humidity.
  FC-28 Soil Hygrometer Module: The FC-28 is a soil hygrometer module that uses the Texas Instruments LM393 comparator chip to provide an analog measurement of soil humidity. The digital output is high when soil moisture is over a certain threshold, as determined by adjusting the potentiometer.
  NodeMCU V3.0: ESP8266 based NodeMCU
